// Logisim project ula.circ as structural Verilog
module mux64 (
  input  Canal_0,
  input  in_2,
  input  in_3,
  input  in_4,
  input  in_5,
  input  in_6,
  input  in_7,
  input  in_8,
  input  in_9,
  input  in_10,
  input  in_11,
  input  in_12,
  input  in_13,
  input  in_14,
  input  in_15,
  input  Canal_15,
  input  in_17,
  input  in_18,
  input  in_19,
  input  in_20,
  input  in_21,
  input  in_22,
  input  in_23,
  input  in_24,
  input  in_25,
  input  in_26,
  input  in_27,
  input  in_28,
  input  in_29,
  input  in_30,
  input  in_31,
  input  in_32,
  input  Canal_32,
  input  in_34,
  input  in_35,
  input  in_36,
  input  in_37,
  input  in_38,
  input  in_39,
  input  in_40,
  input  in_41,
  input  in_42,
  input  in_43,
  input  in_44,
  input  in_45,
  input  in_46,
  input  in_47,
  input  in_48,
  input  Canal_48,
  input  in_50,
  input  in_51,
  input  in_52,
  input  in_53,
  input  in_54,
  input  in_55,
  input  in_56,
  input  in_57,
  input  in_58,
  input  in_59,
  input  in_60,
  input  in_61,
  input  in_62,
  input  in_63,
  input  in_64,
  input  [5:0] Sel,
  output Saida
);

  wire multiplexer_1_out, multiplexer_2_out;

  Multiplexer #(.select(5), .enable("false")) multiplexer_1 (
    .in0(Canal_0), .in1(in_2), .in2(in_3), .in3(in_4), .in4(in_5), .in5(in_6), .in6(in_7), .in7(in_8),
    .in8(in_9), .in9(in_10), .in10(in_11), .in11(in_12), .in12(in_13), .in13(in_14), .in14(in_15),
    .in15(Canal_15), .in16(in_17), .in17(in_18), .in18(in_19), .in19(in_20), .in20(in_21), .in21(in_22),
    .in22(in_23), .in23(in_24), .in24(in_25), .in25(in_26), .in26(in_27), .in27(in_28), .in28(in_29),
    .in29(in_30), .in30(in_31), .in31(in_32), .out(multiplexer_1_out), .sel(Sel[4:0]));
  Multiplexer #(.select(5), .enable("false")) multiplexer_2 (
    .in0(Canal_32), .in1(in_34), .in2(in_35), .in3(in_36), .in4(in_37), .in5(in_38), .in6(in_39),
    .in7(in_40), .in8(in_41), .in9(in_42), .in10(in_43), .in11(in_44), .in12(in_45), .in13(in_46),
    .in14(in_47), .in15(in_48), .in16(Canal_48), .in17(in_50), .in18(in_51), .in19(in_52), .in20(in_53),
    .in21(in_54), .in22(in_55), .in23(in_56), .in24(in_57), .in25(in_58), .in26(in_59), .in27(in_60),
    .in28(in_61), .in29(in_62), .in30(in_63), .in31(in_64), .out(multiplexer_2_out), .sel(Sel[4:0]));
  Multiplexer #(.enable("false")) multiplexer_3 (
    .in0(multiplexer_1_out), .in1(multiplexer_2_out), .out(Saida), .sel(Sel[5]));
endmodule

module CelULA (
  input  CarryIN,
  input  a,
  input  b,
  input  [5:0] OpCode,
  input  [5:0] Function,
  output CarryOUT,
  output out_7
);

  wire A_t, and_1_out, mux64_1_saida, mux64_2_saida, nor_1_out, or_1_out, somadorsubtrator_1_result,
       xor_1_out, zero_1_zerou;

  and and_1 (and_1_out, b, a);
  or or_1 (or_1_out, b, a);
  nor nor_1 (nor_1_out, b, a);
  xor xor_1 (xor_1_out, b, a);
  SomadorSubtrator somadorsubtrator_1 (
    .CarryOUT(CarryOUT), .b(b), .a(a), .SUB(A_t), .Result(somadorsubtrator_1_result), .CarryIN(CarryIN));
  mux64 mux64_1 (
    .in_5(somadorsubtrator_1_result), .in_6(somadorsubtrator_1_result), .in_9(somadorsubtrator_1_result),
    .in_13(and_1_out), .in_14(or_1_out), .in_15(xor_1_out), .in_17(a), .Sel(OpCode), .Saida(mux64_1_saida));  // open: Canal_0, in_2, in_3, in_4, in_7, in_8, in_10, in_11, in_12, Canal_15, in_18, in_19, in_20, in_21, in_22, in_23, in_24, in_25, in_26, in_27, in_28, in_29, in_30, in_31, in_32, Canal_32, in_34, in_35, in_36, in_37, in_38, in_39, in_40, in_41, in_42, in_43, in_44, in_45, in_46, in_47, in_48, Canal_48, in_50, in_51, in_52, in_53, in_54, in_55, in_56, in_57, in_58, in_59, in_60, in_61, in_62, in_63, in_64
  mux64 mux64_2 (
    .Canal_0(a), .in_3(a), .in_4(a), .Canal_32(somadorsubtrator_1_result), .in_35(somadorsubtrator_1_result),
    .in_37(and_1_out), .in_38(or_1_out), .in_39(xor_1_out), .in_40(nor_1_out), .Sel(Function),
    .Saida(mux64_2_saida));  // open: in_2, in_5, in_6, in_7, in_8, in_9, in_10, in_11, in_12, in_13, in_14, in_15, Canal_15, in_17, in_18, in_19, in_20, in_21, in_22, in_23, in_24, in_25, in_26, in_27, in_28, in_29, in_30, in_31, in_32, in_34, in_36, in_41, in_42, in_43, in_44, in_45, in_46, in_47, in_48, Canal_48, in_50, in_51, in_52, in_53, in_54, in_55, in_56, in_57, in_58, in_59, in_60, in_61, in_62, in_63, in_64
  SUB_detector sub_detector_1 (.Subtraction(A_t), .OpCode(OpCode), .Function(Function));
  Zero zero_1 (.In(OpCode), .Zerou(zero_1_zerou));
  Multiplexer #(.enable("false")) multiplexer_1 (
    .in0(mux64_1_saida), .in1(mux64_2_saida), .out(out_7), .sel(zero_1_zerou));
endmodule

module Zero (
  input  [5:0] In,
  output Zerou
);

  nor nor_1 (Zerou, In[0], In[1], In[2], In[4], In[5], In[3]);
endmodule

// Sub D
module SUB_detector (
  input  [5:0] OpCode,
  input  [5:0] Function,
  output Subtraction
);

  wire and_1_out, and_2_out;

  and and_1 (and_1_out, ~OpCode[5], ~OpCode[4], ~OpCode[3], OpCode[2], ~OpCode[1]);  // AND_Gate
  or or_1 (Subtraction, and_1_out, and_2_out);
  and and_2 (and_2_out, ~OpCode[5], ~OpCode[4], ~OpCode[3], ~OpCode[2], ~OpCode[1], ~OpCode[0], Function[5], ~Function[4], ~Function[3], ~Function[2], Function[1], ~Function[0]);  // AND_Gate

  // Notes on the sheet:
  //   Operação
  //   Opcode
  //   sub
  //   000000
  //   beq
  //   000100
  //   000101
  //   bne
  //   Function
  //   000010
  //   xxx
  //   xxx
  //   i
  //   s/z
  //   0
  //   x
  //   1
  //   0
  //   1
  //   0
endmodule

module SomadorSubtrator (
  input  b,
  input  a,
  input  CarryIN,
  input  SUB,
  output CarryOUT,
  output Result
);

  wire multiplexer_1_out, not_1_out;

  not not_1 (not_1_out, b);
  Multiplexer #(.enable("false")) multiplexer_1 (.in0(b), .in1(not_1_out), .out(multiplexer_1_out), .sel(SUB));
  Adder #(.width(1)) adder_1 (.a(a), .b(multiplexer_1_out), .out(Result), .cin(CarryIN), .cout(CarryOUT));
endmodule

module ULA_4_bts (
  input  [4:0] A,
  input  [4:0] B,
  input  [4:0] sa,
  input  [5:0] OpCode,
  input  [5:0] \function ,
  output [4:0] out_6
);

  wire celula_2_carryout, celula_3_carryout, celula_4_carryout, celula_5_carryout, multiplexer_1_out, SL1,
       sub_detector_1_subtraction;
  wire [4:0] deslocadorleft_1_out;

  CelULA celula_1 (
    .b(B[4]), .a(deslocadorleft_1_out[4]), .OpCode(OpCode), .Function(\function ), .out_7(out_6[4]),
    .CarryIN(celula_2_carryout));  // open: CarryOUT
  deslocadorLeft deslocadorleft_1 (.IN(A), .shift_amount(sa), .SL(SL1), .OUT(deslocadorleft_1_out));
  CelULA celula_2 (
    .CarryOUT(celula_2_carryout), .b(B[3]), .a(deslocadorleft_1_out[3]), .OpCode(OpCode),
    .Function(\function ), .out_7(out_6[3]), .CarryIN(celula_3_carryout));
  CelULA celula_3 (
    .CarryOUT(celula_3_carryout), .b(B[2]), .a(deslocadorleft_1_out[2]), .OpCode(OpCode),
    .Function(\function ), .out_7(out_6[2]), .CarryIN(celula_4_carryout));
  CelULA celula_4 (
    .CarryOUT(celula_4_carryout), .b(B[1]), .a(deslocadorleft_1_out[1]), .OpCode(OpCode),
    .Function(\function ), .out_7(out_6[1]), .CarryIN(celula_5_carryout));
  SLL_detect sll_detect_1 (.out_3(SL1), .OpCode(OpCode), .Function(\function ));
  CelULA celula_5 (
    .CarryOUT(celula_5_carryout), .b(B[0]), .a(deslocadorleft_1_out[0]), .OpCode(OpCode),
    .Function(\function ), .out_7(out_6[0]), .CarryIN(multiplexer_1_out));
  Multiplexer #(.enable("false")) multiplexer_1 (
    .in0(1'b0), .in1(1'b1), .out(multiplexer_1_out), .sel(sub_detector_1_subtraction));
  SUB_detector sub_detector_1 (.Subtraction(sub_detector_1_subtraction), .OpCode(OpCode), .Function(\function ));
endmodule

module SLL_detect (
  input  [5:0] OpCode,
  input  [5:0] Function,
  output out_3
);

  nor nor_1 (out_3, OpCode[5], OpCode[4], OpCode[3], OpCode[2], OpCode[1], OpCode[0], Function[5], Function[4], Function[3], Function[2], Function[1], Function[0]);
endmodule

module deslocadorLeft (
  input  [4:0] IN,
  input  SL,
  input  [4:0] shift_amount,
  output [4:0] OUT
);

  wire [4:0] multiplexer_1_out;

  Multiplexer #(.select(5), .width(5), .enable("false")) multiplexer_1 (
    .in0(IN), .in1({IN[3:0], 1'b0}), .in2({IN[2:0], 2'b00}), .in3({IN[1:0], 3'b000}), .in4({IN[0], 4'b0000}),
    .out(multiplexer_1_out), .sel(shift_amount));  // open: in5, in6, in7, in8, in9, in10, in11, in12, in13, in14, in15, in16, in17, in18, in19, in20, in21, in22, in23, in24, in25, in26, in27, in28, in29, in30, in31
  Multiplexer #(.width(5), .enable("false")) multiplexer_2 (.in0(IN), .in1(multiplexer_1_out), .out(OUT), .sel(SL));
endmodule

module SLL (
  input  [31:0] In,
  input  SL,
  input  [4:0] Shift_Amount,
  output [31:0] Out
);

  wire [31:0] multiplexer_1_out;

  Multiplexer #(.select(5), .width(32), .enable("false")) multiplexer_1 (
    .in0(In), .in1({In[30:0], 1'b0}), .in2({In[29:0], 2'b00}), .in3({In[28:0], 3'b000}),
    .in4({In[27:0], 4'b0000}), .in5({In[26:0], {5{1'b0}}}), .in6({In[25:0], {6{1'b0}}}),
    .in7({In[24:0], {7{1'b0}}}), .in8({In[23:0], {8{1'b0}}}), .in9({In[22:0], {9{1'b0}}}),
    .in10({In[21:0], {10{1'b0}}}), .in11({In[20:0], {11{1'b0}}}), .in12({In[19:0], {12{1'b0}}}),
    .in13({In[18:0], {13{1'b0}}}), .in14({In[17:0], {14{1'b0}}}), .in15({In[16:0], {15{1'b0}}}),
    .in16({In[15:0], {16{1'b0}}}), .in17({In[14:0], {17{1'b0}}}), .in18({In[13:0], {18{1'b0}}}),
    .in19({In[12:0], {19{1'b0}}}), .in20({In[11:0], {20{1'b0}}}), .in21({In[10:0], {21{1'b0}}}),
    .in22({In[9:0], {22{1'b0}}}), .in23({In[8:0], {23{1'b0}}}), .in24({In[7:0], {24{1'b0}}}),
    .in25({In[6:0], {25{1'b0}}}), .in26({In[5:0], {26{1'b0}}}), .in27({In[4:0], {27{1'b0}}}),
    .in28({In[3:0], {28{1'b0}}}), .in29({In[2:0], {29{1'b0}}}), .in30({In[1:0], {30{1'b0}}}),
    .in31({In[0], {31{1'b0}}}), .out(multiplexer_1_out), .sel(Shift_Amount));
  Multiplexer #(.width(32), .enable("false")) multiplexer_2 (.in0(In), .in1(multiplexer_1_out), .out(Out), .sel(SL));
endmodule

module ULA32 (
  input  [31:0] A,
  input  [31:0] B,
  input  [4:0] SA,
  input  [5:0] OpCode,
  input  [5:0] Function,
  output ZERO,
  output [31:0] Result
);

  wire celula_1_carryout, celula_3_carryout, celula_4_carryout, celula_5_carryout, celula_6_carryout,
       celula_7_carryout, celula_8_carryout, celula_9_carryout, celula_10_carryout, celula_11_carryout,
       celula_12_carryout, celula_13_carryout, celula_14_carryout, celula_15_carryout, celula_16_carryout,
       celula_17_carryout, celula_18_carryout, celula_19_carryout, celula_20_carryout, celula_21_carryout,
       celula_22_carryout, celula_23_carryout, celula_24_carryout, celula_25_carryout, celula_26_carryout,
       celula_27_carryout, celula_28_carryout, celula_29_carryout, celula_30_carryout, celula_31_carryout,
       celula_32_carryout, multiplexer_1_out, SL1, SR1, SRA1, sub_detector_1_subtraction;
  wire [31:0] sll_1_out, sra_1_out, srl_1_out;

  CelULA celula_1 (
    .CarryOUT(celula_1_carryout), .b(B[15]), .a(sll_1_out[15]), .OpCode(OpCode), .Function(Function),
    .out_7(Result[15]), .CarryIN(celula_4_carryout));
  CelULA celula_2 (
    .b(B[31]), .a(sll_1_out[31]), .OpCode(OpCode), .Function(Function), .out_7(Result[31]),
    .CarryIN(celula_5_carryout));  // open: CarryOUT
  CelULA celula_3 (
    .CarryOUT(celula_3_carryout), .b(B[13]), .a(sll_1_out[13]), .OpCode(OpCode), .Function(Function),
    .out_7(Result[13]), .CarryIN(celula_7_carryout));
  CelULA celula_4 (
    .CarryOUT(celula_4_carryout), .b(B[14]), .a(sll_1_out[14]), .OpCode(OpCode), .Function(Function),
    .out_7(Result[14]), .CarryIN(celula_3_carryout));
  CelULA celula_5 (
    .CarryOUT(celula_5_carryout), .b(B[30]), .a(sll_1_out[30]), .OpCode(OpCode), .Function(Function),
    .out_7(Result[30]), .CarryIN(celula_6_carryout));
  CelULA celula_6 (
    .CarryOUT(celula_6_carryout), .b(B[29]), .a(sll_1_out[29]), .OpCode(OpCode), .Function(Function),
    .out_7(Result[29]), .CarryIN(celula_8_carryout));
  CelULA celula_7 (
    .CarryOUT(celula_7_carryout), .b(B[12]), .a(sll_1_out[12]), .OpCode(OpCode), .Function(Function),
    .out_7(Result[12]), .CarryIN(celula_9_carryout));
  CelULA celula_8 (
    .CarryOUT(celula_8_carryout), .b(B[28]), .a(sll_1_out[28]), .OpCode(OpCode), .Function(Function),
    .out_7(Result[28]), .CarryIN(celula_10_carryout));
  SRA sra_1 (.In(A), .Shift_Amount(SA), .SRA(SRA1), .Out(sra_1_out));
  SRL srl_1 (.In(sra_1_out), .Shift_Amount(SA), .SR(SR1), .Out(srl_1_out));
  CelULA celula_9 (
    .CarryOUT(celula_9_carryout), .b(B[11]), .a(sll_1_out[11]), .OpCode(OpCode), .Function(Function),
    .out_7(Result[11]), .CarryIN(celula_11_carryout));
  CelULA celula_10 (
    .CarryOUT(celula_10_carryout), .b(B[27]), .a(sll_1_out[27]), .OpCode(OpCode), .Function(Function),
    .out_7(Result[27]), .CarryIN(celula_14_carryout));
  SRL_Detect srl_detect_1 (.out_3(SR1), .OpCode(OpCode), .Function(Function));
  SRA_Detect sra_detect_1 (.out_3(SRA1), .OpCode(OpCode), .Function(Function));
  SLL sll_1 (.In(srl_1_out), .Shift_Amount(SA), .SL(SL1), .Out(sll_1_out));
  CelULA celula_11 (
    .CarryOUT(celula_11_carryout), .b(B[10]), .a(sll_1_out[10]), .OpCode(OpCode), .Function(Function),
    .out_7(Result[10]), .CarryIN(celula_12_carryout));
  CelULA celula_12 (
    .CarryOUT(celula_12_carryout), .b(B[9]), .a(sll_1_out[9]), .OpCode(OpCode), .Function(Function),
    .out_7(Result[9]), .CarryIN(celula_15_carryout));
  CelULA celula_13 (
    .CarryOUT(celula_13_carryout), .b(B[25]), .a(sll_1_out[25]), .OpCode(OpCode), .Function(Function),
    .out_7(Result[25]), .CarryIN(celula_16_carryout));
  CelULA celula_14 (
    .CarryOUT(celula_14_carryout), .b(B[26]), .a(sll_1_out[26]), .OpCode(OpCode), .Function(Function),
    .out_7(Result[26]), .CarryIN(celula_13_carryout));
  CelULA celula_15 (
    .CarryOUT(celula_15_carryout), .b(B[8]), .a(sll_1_out[8]), .OpCode(OpCode), .Function(Function),
    .out_7(Result[8]), .CarryIN(celula_17_carryout));
  CelULA celula_16 (
    .CarryOUT(celula_16_carryout), .b(B[24]), .a(sll_1_out[24]), .OpCode(OpCode), .Function(Function),
    .out_7(Result[24]), .CarryIN(celula_18_carryout));
  SLL_detect sll_detect_1 (.out_3(SL1), .OpCode(OpCode), .Function(Function));
  ADDIA addia_1 (.a(sll_1_out));  // open: CarryOUT, in_3, in_4, Result, CarryIN
  CelULA celula_17 (
    .CarryOUT(celula_17_carryout), .b(B[7]), .a(sll_1_out[7]), .OpCode(OpCode), .Function(Function),
    .out_7(Result[7]), .CarryIN(celula_20_carryout));
  CelULA celula_18 (
    .CarryOUT(celula_18_carryout), .b(B[23]), .a(sll_1_out[23]), .OpCode(OpCode), .Function(Function),
    .out_7(Result[23]), .CarryIN(celula_22_carryout));
  CelULA celula_19 (
    .CarryOUT(celula_19_carryout), .b(B[5]), .a(sll_1_out[5]), .OpCode(OpCode), .Function(Function),
    .out_7(Result[5]), .CarryIN(celula_23_carryout));
  CelULA celula_20 (
    .CarryOUT(celula_20_carryout), .b(B[6]), .a(sll_1_out[6]), .OpCode(OpCode), .Function(Function),
    .out_7(Result[6]), .CarryIN(celula_19_carryout));
  CelULA celula_21 (
    .CarryOUT(celula_21_carryout), .b(B[21]), .a(sll_1_out[21]), .OpCode(OpCode), .Function(Function),
    .out_7(Result[21]), .CarryIN(celula_24_carryout));
  CelULA celula_22 (
    .CarryOUT(celula_22_carryout), .b(B[22]), .a(sll_1_out[22]), .OpCode(OpCode), .Function(Function),
    .out_7(Result[22]), .CarryIN(celula_21_carryout));
  CelULA celula_23 (
    .CarryOUT(celula_23_carryout), .b(B[4]), .a(sll_1_out[4]), .OpCode(OpCode), .Function(Function),
    .out_7(Result[4]), .CarryIN(celula_25_carryout));
  CelULA celula_24 (
    .CarryOUT(celula_24_carryout), .b(B[20]), .a(sll_1_out[20]), .OpCode(OpCode), .Function(Function),
    .out_7(Result[20]), .CarryIN(celula_26_carryout));
  CelULA celula_25 (
    .CarryOUT(celula_25_carryout), .b(B[3]), .a(sll_1_out[3]), .OpCode(OpCode), .Function(Function),
    .out_7(Result[3]), .CarryIN(celula_28_carryout));
  CelULA celula_26 (
    .CarryOUT(celula_26_carryout), .b(B[19]), .a(sll_1_out[19]), .OpCode(OpCode), .Function(Function),
    .out_7(Result[19]), .CarryIN(celula_30_carryout));
  CelULA celula_27 (
    .CarryOUT(celula_27_carryout), .b(B[1]), .a(sll_1_out[1]), .OpCode(OpCode), .Function(Function),
    .out_7(Result[1]), .CarryIN(celula_31_carryout));
  CelULA celula_28 (
    .CarryOUT(celula_28_carryout), .b(B[2]), .a(sll_1_out[2]), .OpCode(OpCode), .Function(Function),
    .out_7(Result[2]), .CarryIN(celula_27_carryout));
  CelULA celula_29 (
    .CarryOUT(celula_29_carryout), .b(B[17]), .a(sll_1_out[17]), .OpCode(OpCode), .Function(Function),
    .out_7(Result[17]), .CarryIN(celula_32_carryout));
  CelULA celula_30 (
    .CarryOUT(celula_30_carryout), .b(B[18]), .a(sll_1_out[18]), .OpCode(OpCode), .Function(Function),
    .out_7(Result[18]), .CarryIN(celula_29_carryout));
  CelULA celula_31 (
    .CarryOUT(celula_31_carryout), .b(B[0]), .a(sll_1_out[0]), .OpCode(OpCode), .Function(Function),
    .out_7(Result[0]), .CarryIN(multiplexer_1_out));
  CelULA celula_32 (
    .CarryOUT(celula_32_carryout), .b(B[16]), .a(sll_1_out[16]), .OpCode(OpCode), .Function(Function),
    .out_7(Result[16]), .CarryIN(celula_1_carryout));
  Comparador comparador_1 (.A(sll_1_out), .B(B), .out_3(ZERO));
  Multiplexer #(.enable("false")) multiplexer_1 (
    .in0(1'b0), .in1(1'b1), .out(multiplexer_1_out), .sel(sub_detector_1_subtraction));
  SUB_detector sub_detector_1 (.Subtraction(sub_detector_1_subtraction), .OpCode(OpCode), .Function(Function));

  // Other names for the same wires on the sheet: _13 = Result[13]; _14 = Result[14]; _15 = Result[15]
endmodule

module SRL (
  input  [31:0] In,
  input  SR,
  input  [4:0] Shift_Amount,
  output [31:0] Out
);

  wire [31:0] multiplexer_1_out, shiftright1_1_out_2, shiftright1_2_out_2, shiftright1_3_out_2,
       shiftright1_4_out_2, shiftright1_5_out_2, shiftright1_6_out_2, shiftright1_7_out_2,
       shiftright1_8_out_2, shiftright1_9_out_2, shiftright1_10_out_2, shiftright1_11_out_2,
       shiftright1_12_out_2, shiftright1_13_out_2, shiftright1_14_out_2, shiftright1_15_out_2,
       shiftright1_16_out_2, shiftright1_17_out_2, shiftright1_18_out_2, shiftright1_19_out_2,
       shiftright1_20_out_2, shiftright1_21_out_2, shiftright1_22_out_2, shiftright1_23_out_2,
       shiftright1_24_out_2, shiftright1_25_out_2, shiftright1_26_out_2, shiftright1_27_out_2,
       shiftright1_28_out_2, shiftright1_29_out_2, shiftright1_30_out_2, shiftright1_31_out_2;

  ShiftRight1 shiftright1_1 (.in_1(In), .out_2(shiftright1_1_out_2));
  ShiftRight1 shiftright1_2 (.in_1(shiftright1_1_out_2), .out_2(shiftright1_2_out_2));
  ShiftRight1 shiftright1_3 (.in_1(shiftright1_2_out_2), .out_2(shiftright1_3_out_2));
  ShiftRight1 shiftright1_4 (.in_1(shiftright1_3_out_2), .out_2(shiftright1_4_out_2));
  ShiftRight1 shiftright1_5 (.in_1(shiftright1_4_out_2), .out_2(shiftright1_5_out_2));
  ShiftRight1 shiftright1_6 (.in_1(shiftright1_5_out_2), .out_2(shiftright1_6_out_2));
  ShiftRight1 shiftright1_7 (.in_1(shiftright1_6_out_2), .out_2(shiftright1_7_out_2));
  ShiftRight1 shiftright1_8 (.in_1(shiftright1_7_out_2), .out_2(shiftright1_8_out_2));
  ShiftRight1 shiftright1_9 (.in_1(shiftright1_8_out_2), .out_2(shiftright1_9_out_2));
  ShiftRight1 shiftright1_10 (.in_1(shiftright1_9_out_2), .out_2(shiftright1_10_out_2));
  ShiftRight1 shiftright1_11 (.in_1(shiftright1_10_out_2), .out_2(shiftright1_11_out_2));
  ShiftRight1 shiftright1_12 (.in_1(shiftright1_11_out_2), .out_2(shiftright1_12_out_2));
  ShiftRight1 shiftright1_13 (.in_1(shiftright1_12_out_2), .out_2(shiftright1_13_out_2));
  ShiftRight1 shiftright1_14 (.in_1(shiftright1_13_out_2), .out_2(shiftright1_14_out_2));
  ShiftRight1 shiftright1_15 (.in_1(shiftright1_14_out_2), .out_2(shiftright1_15_out_2));
  ShiftRight1 shiftright1_16 (.in_1(shiftright1_15_out_2), .out_2(shiftright1_16_out_2));
  ShiftRight1 shiftright1_17 (.in_1(shiftright1_16_out_2), .out_2(shiftright1_17_out_2));
  ShiftRight1 shiftright1_18 (.in_1(shiftright1_17_out_2), .out_2(shiftright1_18_out_2));
  ShiftRight1 shiftright1_19 (.in_1(shiftright1_18_out_2), .out_2(shiftright1_19_out_2));
  ShiftRight1 shiftright1_20 (.in_1(shiftright1_19_out_2), .out_2(shiftright1_20_out_2));
  ShiftRight1 shiftright1_21 (.in_1(shiftright1_20_out_2), .out_2(shiftright1_21_out_2));
  ShiftRight1 shiftright1_22 (.in_1(shiftright1_21_out_2), .out_2(shiftright1_22_out_2));
  ShiftRight1 shiftright1_23 (.in_1(shiftright1_22_out_2), .out_2(shiftright1_23_out_2));
  ShiftRight1 shiftright1_24 (.in_1(shiftright1_23_out_2), .out_2(shiftright1_24_out_2));
  ShiftRight1 shiftright1_25 (.in_1(shiftright1_24_out_2), .out_2(shiftright1_25_out_2));
  ShiftRight1 shiftright1_26 (.in_1(shiftright1_25_out_2), .out_2(shiftright1_26_out_2));
  ShiftRight1 shiftright1_27 (.in_1(shiftright1_26_out_2), .out_2(shiftright1_27_out_2));
  ShiftRight1 shiftright1_28 (.in_1(shiftright1_27_out_2), .out_2(shiftright1_28_out_2));
  ShiftRight1 shiftright1_29 (.in_1(shiftright1_28_out_2), .out_2(shiftright1_29_out_2));
  ShiftRight1 shiftright1_30 (.in_1(shiftright1_29_out_2), .out_2(shiftright1_30_out_2));
  ShiftRight1 shiftright1_31 (.in_1(shiftright1_30_out_2), .out_2(shiftright1_31_out_2));
  Multiplexer #(.select(5), .width(32), .enable("false")) multiplexer_1 (
    .in0(In), .in1(shiftright1_1_out_2), .in2(shiftright1_2_out_2), .in3(shiftright1_3_out_2),
    .in4(shiftright1_4_out_2), .in5(shiftright1_5_out_2), .in6(shiftright1_6_out_2),
    .in7(shiftright1_7_out_2), .in8(shiftright1_8_out_2), .in9(shiftright1_9_out_2),
    .in10(shiftright1_10_out_2), .in11(shiftright1_11_out_2), .in12(shiftright1_12_out_2),
    .in13(shiftright1_13_out_2), .in14(shiftright1_14_out_2), .in15(shiftright1_15_out_2),
    .in16(shiftright1_16_out_2), .in17(shiftright1_17_out_2), .in18(shiftright1_18_out_2),
    .in19(shiftright1_19_out_2), .in20(shiftright1_20_out_2), .in21(shiftright1_21_out_2),
    .in22(shiftright1_22_out_2), .in23(shiftright1_23_out_2), .in24(shiftright1_24_out_2),
    .in25(shiftright1_25_out_2), .in26(shiftright1_26_out_2), .in27(shiftright1_27_out_2),
    .in28(shiftright1_28_out_2), .in29(shiftright1_29_out_2), .in30(shiftright1_30_out_2),
    .in31(shiftright1_31_out_2), .out(multiplexer_1_out), .sel(Shift_Amount));
  Multiplexer #(.width(32), .enable("false")) multiplexer_2 (.in0(In), .in1(multiplexer_1_out), .out(Out), .sel(SR));
endmodule

module ShiftRight1 (
  input  [31:0] in_1,
  output [31:0] out_2
);


  assign out_2 = {1'b0, in_1[31:1]};
endmodule

module ShiftRightA (
  input  [31:0] in_1,
  output [31:0] out_2
);


  assign out_2 = {{2{in_1[31]}}, in_1[30:1]};
endmodule

module BR2 (
  input  [31:0] DataIn,
  input  SAVE,
  input  Write_Enable,
  input  Reset,
  input  [4:0] RegW,
  input  [4:0] RegS,
  input  [4:0] RegT,
  output [31:0] DadoRegS,
  output [31:0] DadoRegT
);

  wire _1, _2, _3, _4, _5, _6, _7, _8, _9, _10, _11, _12, _13, _14, _15, _16, _17, _18, _19, _20, _21, _22,
       _23, _24, _25, _26, _27, _28, _29, _30, _31, and_1_out;
  wire [31:0] _1A, _2A, _3A, _4A, _5A, _6A, _7A, _8A, _9A, _10A, _11A, _12A, _13A, _14A, _15A, _16A, _17A,
       _18A, _19A, _20A, _21A, _22A, _23A, _24A, _25A, _26A, _27A, _28A, _29A, _30A, _31A;

  and and_1 (and_1_out, SAVE, Write_Enable);
  Demultiplexer #(.select(5), .enable("false")) demultiplexer_1 (
    .out1(_1), .out2(_2), .out3(_3), .out4(_4), .out5(_5), .out6(_6), .out7(_7), .out8(_8), .out9(_9),
    .out10(_10), .out11(_11), .out12(_12), .out13(_13), .out14(_14), .out15(_15), .out16(_16), .out17(_17),
    .out18(_18), .out19(_19), .out20(_20), .out21(_21), .out22(_22), .out23(_23), .out24(_24), .out25(_25),
    .out26(_26), .out27(_27), .out28(_28), .out29(_29), .out30(_30), .out31(_31), .in(and_1_out), .sel(RegW));  // open: out0
  Register #(.width(32)) register_1 (.D(DataIn), .Q(_4A), .clk(_4), .clr(Reset));  // open: en
  Register #(.width(32)) register_2 (.D(DataIn), .Q(_8A), .clk(_8), .clr(Reset));  // open: en
  Register #(.width(32)) register_3 (.D(DataIn), .Q(_12A), .clk(_12), .clr(Reset));  // open: en
  Register #(.width(32)) register_4 (.D(DataIn), .Q(_16A), .clk(_16), .clr(Reset));  // open: en
  Register #(.width(32)) register_5 (.D(DataIn), .Q(_20A), .clk(_20), .clr(Reset));  // open: en
  Register #(.width(32)) register_6 (.D(DataIn), .Q(_24A), .clk(_24), .clr(Reset));  // open: en
  Register #(.width(32)) register_7 (.D(DataIn), .Q(_28A), .clk(_28), .clr(Reset));  // open: en
  Register #(.width(32)) register_8 (.D(DataIn), .Q(_1A), .clk(_1), .clr(Reset));  // open: en
  Register #(.width(32)) register_9 (.D(DataIn), .Q(_5A), .clk(_5), .clr(Reset));  // open: en
  Register #(.width(32)) register_10 (.D(DataIn), .Q(_9A), .clk(_9), .clr(Reset));  // open: en
  Register #(.width(32)) register_11 (.D(DataIn), .Q(_13A), .clk(_13), .clr(Reset));  // open: en
  Register #(.width(32)) register_12 (.D(DataIn), .Q(_17A), .clk(_17), .clr(Reset));  // open: en
  Register #(.width(32)) register_13 (.D(DataIn), .Q(_21A), .clk(_21), .clr(Reset));  // open: en
  Register #(.width(32)) register_14 (.D(DataIn), .Q(_25A), .clk(_25), .clr(Reset));  // open: en
  Register #(.width(32)) register_15 (.D(DataIn), .Q(_29A), .clk(_29), .clr(Reset));  // open: en
  Register #(.width(32)) register_16 (.D(DataIn), .Q(_2A), .clk(_2), .clr(Reset));  // open: en
  Register #(.width(32)) register_17 (.D(DataIn), .Q(_6A), .clk(_6), .clr(Reset));  // open: en
  Register #(.width(32)) register_18 (.D(DataIn), .Q(_10A), .clk(_10), .clr(Reset));  // open: en
  Register #(.width(32)) register_19 (.D(DataIn), .Q(_14A), .clk(_14), .clr(Reset));  // open: en
  Register #(.width(32)) register_20 (.D(DataIn), .Q(_18A), .clk(_18), .clr(Reset));  // open: en
  Register #(.width(32)) register_21 (.D(DataIn), .Q(_22A), .clk(_22), .clr(Reset));  // open: en
  Register #(.width(32)) register_22 (.D(DataIn), .Q(_26A), .clk(_26), .clr(Reset));  // open: en
  Register #(.width(32)) register_23 (.D(DataIn), .Q(_30A), .clk(_30), .clr(Reset));  // open: en
  Register #(.width(32)) register_24 (.D(DataIn), .Q(_3A), .clk(_3), .clr(Reset));  // open: en
  Register #(.width(32)) register_25 (.D(DataIn), .Q(_7A), .clk(_7), .clr(Reset));  // open: en
  Register #(.width(32)) register_26 (.D(DataIn), .Q(_11A), .clk(_11), .clr(Reset));  // open: en
  Register #(.width(32)) register_27 (.D(DataIn), .Q(_15A), .clk(_15), .clr(Reset));  // open: en
  Register #(.width(32)) register_28 (.D(DataIn), .Q(_19A), .clk(_19), .clr(Reset));  // open: en
  Register #(.width(32)) register_29 (.D(DataIn), .Q(_23A), .clk(_23), .clr(Reset));  // open: en
  Register #(.width(32)) register_30 (.D(DataIn), .Q(_27A), .clk(_27), .clr(Reset));  // open: en
  Register #(.width(32)) register_31 (.D(DataIn), .Q(_31A), .clk(_31), .clr(Reset));  // open: en
  Multiplexer #(.select(5), .width(32), .enable("false")) multiplexer_1 (
    .in0({32{1'b0}}), .in1(_1A), .in2(_2A), .in3(_3A), .in4(_4A), .in5(_5A), .in6(_6A), .in7(_7A), .in8(_8A),
    .in9(_9A), .in10(_10A), .in11(_11A), .in12(_12A), .in13(_13A), .in14(_14A), .in15(_15A), .in16(_16A),
    .in17(_17A), .in18(_18A), .in19(_19A), .in20(_20A), .in21(_21A), .in22(_22A), .in23(_23A), .in24(_24A),
    .in25(_25A), .in26(_26A), .in27(_27A), .in28(_28A), .in29(_29A), .in30(_30A), .in31(_31A),
    .out(DadoRegS), .sel(RegS));
  Multiplexer #(.select(5), .width(32), .enable("false")) multiplexer_2 (
    .in0({32{1'b0}}), .in1(_1A), .in2(_2A), .in3(_3A), .in4(_4A), .in5(_5A), .in6(_6A), .in7(_7A), .in8(_8A),
    .in9(_9A), .in10(_10A), .in11(_11A), .in12(_12A), .in13(_13A), .in14(_14A), .in15(_15A), .in16(_16A),
    .in17(_17A), .in18(_18A), .in19(_19A), .in20(_20A), .in21(_21A), .in22(_22A), .in23(_23A), .in24(_24A),
    .in25(_25A), .in26(_26A), .in27(_27A), .in28(_28A), .in29(_29A), .in30(_30A), .in31(_31A),
    .out(DadoRegT), .sel(RegT));
endmodule

module SRA (
  input  [31:0] In,
  input  SRA,
  input  [4:0] Shift_Amount,
  output [31:0] Out
);

  wire [31:0] multiplexer_1_out, shiftrighta_1_out_2, shiftrighta_2_out_2, shiftrighta_3_out_2,
       shiftrighta_4_out_2, shiftrighta_5_out_2, shiftrighta_6_out_2, shiftrighta_7_out_2,
       shiftrighta_8_out_2, shiftrighta_9_out_2, shiftrighta_10_out_2, shiftrighta_11_out_2,
       shiftrighta_12_out_2, shiftrighta_13_out_2, shiftrighta_14_out_2, shiftrighta_15_out_2,
       shiftrighta_16_out_2, shiftrighta_17_out_2, shiftrighta_18_out_2, shiftrighta_19_out_2,
       shiftrighta_20_out_2, shiftrighta_21_out_2, shiftrighta_22_out_2, shiftrighta_23_out_2,
       shiftrighta_24_out_2, shiftrighta_25_out_2, shiftrighta_26_out_2, shiftrighta_27_out_2,
       shiftrighta_28_out_2, shiftrighta_29_out_2, shiftrighta_30_out_2, shiftrighta_31_out_2;

  ShiftRightA shiftrighta_1 (.in_1(In), .out_2(shiftrighta_1_out_2));
  ShiftRightA shiftrighta_2 (.in_1(shiftrighta_1_out_2), .out_2(shiftrighta_2_out_2));
  ShiftRightA shiftrighta_3 (.in_1(shiftrighta_2_out_2), .out_2(shiftrighta_3_out_2));
  ShiftRightA shiftrighta_4 (.in_1(shiftrighta_3_out_2), .out_2(shiftrighta_4_out_2));
  ShiftRightA shiftrighta_5 (.in_1(shiftrighta_4_out_2), .out_2(shiftrighta_5_out_2));
  ShiftRightA shiftrighta_6 (.in_1(shiftrighta_5_out_2), .out_2(shiftrighta_6_out_2));
  ShiftRightA shiftrighta_7 (.in_1(shiftrighta_6_out_2), .out_2(shiftrighta_7_out_2));
  ShiftRightA shiftrighta_8 (.in_1(shiftrighta_7_out_2), .out_2(shiftrighta_8_out_2));
  ShiftRightA shiftrighta_9 (.in_1(shiftrighta_8_out_2), .out_2(shiftrighta_9_out_2));
  ShiftRightA shiftrighta_10 (.in_1(shiftrighta_9_out_2), .out_2(shiftrighta_10_out_2));
  ShiftRightA shiftrighta_11 (.in_1(shiftrighta_10_out_2), .out_2(shiftrighta_11_out_2));
  ShiftRightA shiftrighta_12 (.in_1(shiftrighta_11_out_2), .out_2(shiftrighta_12_out_2));
  ShiftRightA shiftrighta_13 (.in_1(shiftrighta_12_out_2), .out_2(shiftrighta_13_out_2));
  ShiftRightA shiftrighta_14 (.in_1(shiftrighta_13_out_2), .out_2(shiftrighta_14_out_2));
  ShiftRightA shiftrighta_15 (.in_1(shiftrighta_14_out_2), .out_2(shiftrighta_15_out_2));
  ShiftRightA shiftrighta_16 (.in_1(shiftrighta_15_out_2), .out_2(shiftrighta_16_out_2));
  ShiftRightA shiftrighta_17 (.in_1(shiftrighta_16_out_2), .out_2(shiftrighta_17_out_2));
  ShiftRightA shiftrighta_18 (.in_1(shiftrighta_17_out_2), .out_2(shiftrighta_18_out_2));
  ShiftRightA shiftrighta_19 (.in_1(shiftrighta_18_out_2), .out_2(shiftrighta_19_out_2));
  ShiftRightA shiftrighta_20 (.in_1(shiftrighta_19_out_2), .out_2(shiftrighta_20_out_2));
  ShiftRightA shiftrighta_21 (.in_1(shiftrighta_20_out_2), .out_2(shiftrighta_21_out_2));
  ShiftRightA shiftrighta_22 (.in_1(shiftrighta_21_out_2), .out_2(shiftrighta_22_out_2));
  ShiftRightA shiftrighta_23 (.in_1(shiftrighta_22_out_2), .out_2(shiftrighta_23_out_2));
  ShiftRightA shiftrighta_24 (.in_1(shiftrighta_23_out_2), .out_2(shiftrighta_24_out_2));
  ShiftRightA shiftrighta_25 (.in_1(shiftrighta_24_out_2), .out_2(shiftrighta_25_out_2));
  ShiftRightA shiftrighta_26 (.in_1(shiftrighta_25_out_2), .out_2(shiftrighta_26_out_2));
  ShiftRightA shiftrighta_27 (.in_1(shiftrighta_26_out_2), .out_2(shiftrighta_27_out_2));
  ShiftRightA shiftrighta_28 (.in_1(shiftrighta_27_out_2), .out_2(shiftrighta_28_out_2));
  ShiftRightA shiftrighta_29 (.in_1(shiftrighta_28_out_2), .out_2(shiftrighta_29_out_2));
  ShiftRightA shiftrighta_30 (.in_1(shiftrighta_29_out_2), .out_2(shiftrighta_30_out_2));
  ShiftRightA shiftrighta_31 (.in_1(shiftrighta_30_out_2), .out_2(shiftrighta_31_out_2));
  Multiplexer #(.select(5), .width(32), .enable("false")) multiplexer_1 (
    .in0(In), .in1(shiftrighta_1_out_2), .in2(shiftrighta_2_out_2), .in3(shiftrighta_3_out_2),
    .in4(shiftrighta_4_out_2), .in5(shiftrighta_5_out_2), .in6(shiftrighta_6_out_2),
    .in7(shiftrighta_7_out_2), .in8(shiftrighta_8_out_2), .in9(shiftrighta_9_out_2),
    .in10(shiftrighta_10_out_2), .in11(shiftrighta_11_out_2), .in12(shiftrighta_12_out_2),
    .in13(shiftrighta_13_out_2), .in14(shiftrighta_14_out_2), .in15(shiftrighta_15_out_2),
    .in16(shiftrighta_16_out_2), .in17(shiftrighta_17_out_2), .in18(shiftrighta_18_out_2),
    .in19(shiftrighta_19_out_2), .in20(shiftrighta_20_out_2), .in21(shiftrighta_21_out_2),
    .in22(shiftrighta_22_out_2), .in23(shiftrighta_23_out_2), .in24(shiftrighta_24_out_2),
    .in25(shiftrighta_25_out_2), .in26(shiftrighta_26_out_2), .in27(shiftrighta_27_out_2),
    .in28(shiftrighta_28_out_2), .in29(shiftrighta_29_out_2), .in30(shiftrighta_30_out_2),
    .in31(shiftrighta_31_out_2), .out(multiplexer_1_out), .sel(Shift_Amount));
  Multiplexer #(.width(32), .enable("false")) multiplexer_2 (.in0(In), .in1(multiplexer_1_out), .out(Out), .sel(SRA));
endmodule

// Seleto
module Deslocadores (
  input  [31:0] In,
  input  SLL,
  input  SRL,
  input  SRA,
  input  [4:0] in_5,
  output [31:0] Out
);

  wire [31:0] sll_1_out, sll_2_out, sra_1_out;

  SLL sll_1 (.In(In), .Shift_Amount(in_5), .SL(SLL), .Out(sll_1_out));
  SLL sll_2 (.In(In), .Shift_Amount(in_5), .SL(SRL), .Out(sll_2_out));
  SRA sra_1 (.In(In), .Shift_Amount(in_5), .SRA(SRA), .Out(sra_1_out));
  Multiplexer #(.select(3), .width(32), .enable("false")) multiplexer_1 (
    .in0(sll_1_out), .in1(sll_2_out), .in2(sra_1_out), .out(Out), .sel({SRA, SRL, SLL}));  // open: in3, in4, in5, in6, in7
endmodule

module SRL_Detect (
  input  [5:0] OpCode,
  input  [5:0] Function,
  output out_3
);

  nor nor_1 (out_3, OpCode[5], OpCode[4], OpCode[3], OpCode[2], OpCode[1], OpCode[0], Function[5], Function[4], Function[3], Function[2], ~Function[1], Function[0]);  // NOR_Gate
endmodule

module SRA_Detect (
  input  [5:0] OpCode,
  input  [5:0] Function,
  output out_3
);

  nor nor_1 (out_3, OpCode[5], OpCode[4], OpCode[3], OpCode[2], OpCode[1], OpCode[0], Function[5], Function[4], Function[3], Function[2], ~Function[1], ~Function[0]);  // NOR_Gate
endmodule

module Comparador (
  input  [31:0] A,
  input  [31:0] B,
  output out_3
);

  wire xor_1_out, xor_2_out, xor_3_out, xor_4_out, xor_5_out, xor_6_out, xor_7_out, xor_8_out, xor_9_out,
       xor_10_out, xor_11_out, xor_12_out, xor_13_out, xor_14_out, xor_15_out, xor_16_out, xor_17_out,
       xor_18_out, xor_19_out, xor_20_out, xor_21_out, xor_22_out, xor_23_out, xor_24_out, xor_25_out,
       xor_26_out, xor_27_out, xor_28_out, xor_29_out, xor_30_out, xor_31_out, xor_32_out;

  xor xor_1 (xor_1_out, B[30], A[30]);
  xor xor_2 (xor_2_out, B[31], A[31]);
  xor xor_3 (xor_3_out, B[29], A[29]);
  xor xor_4 (xor_4_out, B[28], A[28]);
  xor xor_5 (xor_5_out, B[27], A[27]);
  xor xor_6 (xor_6_out, B[26], A[26]);
  xor xor_7 (xor_7_out, B[24], A[24]);
  xor xor_8 (xor_8_out, B[25], A[25]);
  xor xor_9 (xor_9_out, B[22], A[22]);
  xor xor_10 (xor_10_out, B[23], A[23]);
  xor xor_11 (xor_11_out, B[20], A[20]);
  xor xor_12 (xor_12_out, B[21], A[21]);
  xor xor_13 (xor_13_out, B[18], A[18]);
  xor xor_14 (xor_14_out, B[19], A[19]);
  xor xor_15 (xor_15_out, B[17], A[17]);
  xor xor_16 (xor_16_out, B[16], A[16]);
  xor xor_17 (xor_17_out, B[15], A[15]);
  xor xor_18 (xor_18_out, B[14], A[14]);
  xor xor_19 (xor_19_out, B[13], A[13]);
  xor xor_20 (xor_20_out, B[12], A[12]);
  nor nor_1 (out_3, xor_2_out, xor_1_out, xor_3_out, xor_4_out, xor_5_out, xor_6_out, xor_8_out, xor_7_out, xor_10_out, xor_9_out, xor_12_out, xor_11_out, xor_14_out, xor_13_out, xor_15_out, xor_16_out, xor_17_out, xor_18_out, xor_19_out, xor_20_out, xor_21_out, xor_22_out, xor_23_out, xor_24_out, xor_26_out, xor_25_out, xor_27_out, xor_28_out, xor_30_out, xor_29_out, xor_31_out, xor_32_out);
  xor xor_21 (xor_21_out, B[11], A[11]);
  xor xor_22 (xor_22_out, B[10], A[10]);
  xor xor_23 (xor_23_out, B[9], A[9]);
  xor xor_24 (xor_24_out, B[8], A[8]);
  xor xor_25 (xor_25_out, B[6], A[6]);
  xor xor_26 (xor_26_out, B[7], A[7]);
  xor xor_27 (xor_27_out, B[5], A[5]);
  xor xor_28 (xor_28_out, B[4], A[4]);
  xor xor_29 (xor_29_out, B[2], A[2]);
  xor xor_30 (xor_30_out, B[3], A[3]);
  xor xor_31 (xor_31_out, B[1], A[1]);
  xor xor_32 (xor_32_out, B[0], A[0]);
endmodule

module ADDIA (
  input  [31:0] a,
  input  CarryIN,
  input  in_3,
  input  [4:0] in_4,
  output CarryOUT,
  output [31:0] Result
);

  wire [31:0] demultiplexer_1_out0;

  Demultiplexer #(.select(5), .enable("false")) demultiplexer_1 (
    .out0(demultiplexer_1_out0[0]), .out1(demultiplexer_1_out0[1]), .out2(demultiplexer_1_out0[2]),
    .out3(demultiplexer_1_out0[3]), .out4(demultiplexer_1_out0[4]), .out5(demultiplexer_1_out0[5]),
    .out6(demultiplexer_1_out0[6]), .out7(demultiplexer_1_out0[7]), .out8(demultiplexer_1_out0[8]),
    .out9(demultiplexer_1_out0[9]), .out10(demultiplexer_1_out0[10]), .out11(demultiplexer_1_out0[11]),
    .out12(demultiplexer_1_out0[12]), .out13(demultiplexer_1_out0[13]), .out14(demultiplexer_1_out0[14]),
    .out15(demultiplexer_1_out0[15]), .out16(demultiplexer_1_out0[16]), .out17(demultiplexer_1_out0[17]),
    .out18(demultiplexer_1_out0[18]), .out19(demultiplexer_1_out0[19]), .out20(demultiplexer_1_out0[20]),
    .out21(demultiplexer_1_out0[21]), .out22(demultiplexer_1_out0[22]), .out23(demultiplexer_1_out0[23]),
    .out24(demultiplexer_1_out0[24]), .out25(demultiplexer_1_out0[25]), .out26(demultiplexer_1_out0[26]),
    .out27(demultiplexer_1_out0[27]), .out28(demultiplexer_1_out0[28]), .out29(demultiplexer_1_out0[29]),
    .out30(demultiplexer_1_out0[30]), .out31(demultiplexer_1_out0[31]), .in(in_3), .sel(in_4));
  Adder #(.width(32)) adder_1 (.a(a), .b(demultiplexer_1_out0), .out(Result), .cin(CarryIN), .cout(CarryOUT));
endmodule

module UsoBR (
  input  [31:0] DadoIn,
  input  in_2,
  input  in_3,
  input  [4:0] RW,
  input  [4:0] RT,
  input  [4:0] RS,
  output [31:0] DadoS,
  output [31:0] DadoT
);

  // BR2 br2_1: pin names not known; wires that end beside it: in_3, in_2, RW, DadoIn, RS, RT, DadoS, DadoT
endmodule

module Sign_ext (
  input  Sign___Zero,
  input  [15:0] In16,
  output [31:0] Out32
);

  Multiplexer #(.enable("false")) multiplexer_1 (.in0(1'b0), .in1(In16[15]), .out(Out32[31]), .sel(Sign___Zero));

  assign Out32[30:0] = {{15{Out32[31]}}, In16};
endmodule

module Via_de_dados (
  input  Reset,
  input  Clock,
  input  [31:0] in_3,
  output [31:0] ADDR,
  output [31:0] Instruction
);

  wire BR, EN_W, i, not_1_out, s_z, ula32_1_zero;
  wire [4:0] RS_Con, RT_Con, RW_Con, SA_Con;
  wire [5:0] Function_Con, OpCode_Con;
  wire [15:0] IMM_Con;
  wire [31:0] br2_1_dadoregs, br2_1_dadoregt, multiplexer_1_out, sign_ext_1_out32, ula32_1_result;

  PC_NOVO pc_novo_1 (
    .Clock(not_1_out), .Reset(Reset), .Offset(sign_ext_1_out32), .BR(BR), .Equals(ula32_1_zero), .Addr(ADDR));
  not not_1 (not_1_out, Clock);
  BR2 br2_1 (
    .DadoRegS(br2_1_dadoregs), .DadoRegT(br2_1_dadoregt), .Reset(Reset), .RegS(RS_Con), .RegT(RT_Con),
    .SAVE(Clock), .Write_Enable(EN_W), .DataIn(ula32_1_result), .RegW(RW_Con));
  Unidade_de_Controle unidade_de_controle_1 (
    .Instruction(Instruction), .IMM(IMM_Con), .Function(Function_Con), .SA(SA_Con), .RW(RW_Con), .RT(RT_Con),
    .RS(RS_Con), .OpCode(OpCode_Con), .i(i), .s_z(s_z), .RegWrite_Enable(EN_W), .Branch(BR));
  Multiplexer #(.width(32), .enable("false")) multiplexer_1 (
    .in0(br2_1_dadoregt), .in1(sign_ext_1_out32), .out(multiplexer_1_out), .sel(i));
  Sign_ext sign_ext_1 (.Sign___Zero(s_z), .Out32(sign_ext_1_out32), .In16(IMM_Con));
  ULA32 ula32_1 (
    .A(br2_1_dadoregs), .B(multiplexer_1_out), .SA(SA_Con), .Result(ula32_1_result), .ZERO(ula32_1_zero),
    .OpCode(OpCode_Con), .Function(Function_Con));
  RAM #(.dataWidth(32)) ram_1 (.addr(ADDR[9:2]), .data(Instruction));  // open: sel, clk, ld, clr

  // Other names for the same wires on the sheet: MEMAddr[31:0] = ADDR; MEMInst[31:0] = Instruction

  // Notes on the sheet:
  //   31    26
  //   Opcode
  //   Opcode
  //   Operação
  //   addi
  //   andi
  //   ori
  //   xori
  //   sll
  //   srl
  //   sra
  //   add
  //   and
  //   or
  //   xor
  //   nor
  //   beq
  //   bne
  //   25  21
  //   RT
  //   RS
  //   RS
  //   RT
  //   CODIGOS
  //   Opcode
  //   001000
  //   001100
  //   001101
  //   001110
  //   000000
  //   000000
  //   000000
  //   000000
  //   000000
  //   000000
  //   000000
  //   000000
  //   000100
  //   000101
  //   20  16
  //   15  11
  //   10  6
  //   RW
  //   RT no type I escolhe onde será gravado (substitui o RW)
  //   Function
  //   in I
  //   xxx
  //   1
  //   xxx
  //   1
  //   xxx
  //   1
  //   xxx
  //   1
  //   000000
  //   0
  //   0
  //   000010
  //   0
  //   000011
  //   0
  //   100000
  //   0
  //   100100
  //   0
  //   100101
  //   0
  //   100110
  //   0
  //   100111
  //   xxx
  //   0
  //   xxx
  //   0
  //   5    0
  //   Function
  //   SA
  //   Immediate
  //   S / Z
  //   1
  //   0
  //   0
  //   0
  //   x
  //   x
  //   x
  //   x
  //   x
  //   x
  //   x
  //   x
  //   1
  //   1
  //   Type R
  //   Type I
  //   MicroProcessador
  //   Memoria
endmodule

// I
module Signal___I (
  input  [5:0] OpCode,
  output Signal___I
);

  wire and_1_out, not_1_out, or_1_out;

  and and_1 (and_1_out, ~OpCode[5], ~OpCode[4], ~OpCode[3], OpCode[2], ~OpCode[1]);  // AND_Gate
  and and_2 (Signal___I, not_1_out, or_1_out);
  not not_1 (not_1_out, and_1_out);
  or or_1 (or_1_out, OpCode[3], OpCode[5], OpCode[4], OpCode[2], OpCode[1], OpCode[0]);
endmodule

// Sign S/Z
module Signal___S___Z (
  input  [5:0] OpCode,
  output out_2
);

  wire and_1_out, and_2_out, and_3_out;

  and and_1 (and_1_out, ~OpCode[5], ~OpCode[4], OpCode[3], ~OpCode[2], ~OpCode[1], ~OpCode[0]);  // AND_Gate
  or or_1 (out_2, and_1_out, and_2_out, and_3_out);
  and and_2 (and_2_out, ~OpCode[5], ~OpCode[4], ~OpCode[3], OpCode[2], ~OpCode[1], ~OpCode[0]);  // AND_Gate
  and and_3 (and_3_out, ~OpCode[5], ~OpCode[4], ~OpCode[3], OpCode[2], ~OpCode[1], OpCode[0]);  // AND_Gate
endmodule

module Comparador_Igualdade (
  input  [31:0] in_1,
  input  [31:0] in_2,
  output Iquals,
  output Not_Iquals
);

  wire [31:0] xnor_1_out;

  assign xnor_1_out = ~(in_1 ^ in_2);  // XNOR_Gate xnor_1, 32 bits wide
  and and_1 (Iquals, xnor_1_out[0], xnor_1_out[1], xnor_1_out[2], xnor_1_out[3], xnor_1_out[4], xnor_1_out[5], xnor_1_out[6], xnor_1_out[7], xnor_1_out[8], xnor_1_out[9], xnor_1_out[10], xnor_1_out[11], xnor_1_out[12], xnor_1_out[13], xnor_1_out[14], xnor_1_out[15], xnor_1_out[17], xnor_1_out[18], xnor_1_out[19], xnor_1_out[20], xnor_1_out[21], xnor_1_out[22], xnor_1_out[23], xnor_1_out[24], xnor_1_out[25], xnor_1_out[26], xnor_1_out[27], xnor_1_out[28], xnor_1_out[29], xnor_1_out[30], xnor_1_out[31], xnor_1_out[16]);
  not not_1 (Not_Iquals, Iquals);
endmodule

// Un Control
module Unidade_de_Controle (
  input  [31:0] Instruction,
  output [15:0] IMM,
  output [5:0] Function,
  output [4:0] SA,
  output [4:0] RW,
  output [4:0] RT,
  output [4:0] RS,
  output [5:0] OpCode,
  output i,
  output s_z,
  output RegWrite_Enable,
  output Branch
);

  Signal___I signal___i_1 (.Signal___I(i), .OpCode(Instruction[31:26]));
  Signal___S___Z signal___s_z_1 (.out_2(s_z), .OpCode(Instruction[31:26]));
  Write_Enable_Detect write_enable_detect_1 (.OpCode(Instruction[31:26]), .Write(RegWrite_Enable));
  BR_detect br_detect_1 (.OpCode(Instruction[31:26]), .Write(Branch));
  Multiplexer #(.width(5), .enable("false")) multiplexer_1 (
    .in0(Instruction[15:11]), .in1(Instruction[20:16]), .out(RW), .sel(i));

  assign Function = Instruction[5:0];
  assign IMM = Instruction[15:0];
  assign OpCode = Instruction[31:26];
  assign RS = Instruction[25:21];
  assign RT = Instruction[20:16];
  assign SA = Instruction[10:6];

  // Notes on the sheet:
  //   31    26
  //   Opcode
  //   Opcode
  //   20  16
  //   25  21
  //   RT
  //   RS
  //   RS
  //   RT
  //   10  6
  //   15  11
  //   SA
  //   RW
  //   Immediate
  //   RT no type I escolhe onde será gravado (substitui o RW)
  //   5    0
  //   Type R
  //   Function
  //   Type I
endmodule

// RAM
module MemRam (
  input  [31:0] ADDR,
  output [31:0] Instruction
);

  RAM #(.dataWidth(32)) ram_1 (.addr(ADDR[9:2]), .data(Instruction));  // open: sel, clk, ld, clr
endmodule

// PC
module Program_Counter__PC (
  input  Clock,
  input  Reset,
  output [31:0] ADDR
);

  wire [31:0] adder_1_out;

  Register #(.width(32)) register_1 (.D(adder_1_out), .Q(ADDR), .clk(Clock), .clr(Reset));  // open: en
  Adder #(.width(32)) adder_1 (.a(32'h4), .b(ADDR), .out(adder_1_out));  // open: cin, cout
endmodule

// WE
module Write_Enable_Detect (
  input  [5:0] OpCode,
  output Write
);

  wire and_1_out, and_2_out;

  and and_1 (and_1_out, ~OpCode[0], ~OpCode[1], OpCode[2], ~OpCode[3], ~OpCode[4], ~OpCode[5]);  // AND_Gate
  and and_2 (and_2_out, OpCode[0], ~OpCode[1], OpCode[2], ~OpCode[3], ~OpCode[4], ~OpCode[5]);  // AND_Gate
  nor nor_1 (Write, and_1_out, and_2_out);
endmodule

// BR
module BR_detect (
  input  [5:0] OpCode,
  output Write
);

  wire and_1_out, and_2_out;

  and and_1 (and_1_out, ~OpCode[0], ~OpCode[1], OpCode[2], ~OpCode[3], ~OpCode[4], ~OpCode[5]);  // AND_Gate
  and and_2 (and_2_out, OpCode[0], ~OpCode[1], OpCode[2], ~OpCode[3], ~OpCode[4], ~OpCode[5]);  // AND_Gate
  or or_1 (Write, and_1_out, and_2_out);
endmodule

// PC
module PC_NOVO (
  input  [31:0] Offset,
  input  BR,
  input  Equals,
  input  Clock,
  input  Reset,
  output [31:0] Addr
);

  wire and_1_out;
  wire [31:0] adder_1_out, adder_2_out, multiplexer_1_out;

  Adder #(.width(32)) adder_1 (.a({Offset[29:0], 2'b00}), .b(32'h4), .out(adder_1_out));  // open: cin, cout
  Multiplexer #(.width(32), .enable("false")) multiplexer_1 (
    .in0(32'h4), .in1(adder_1_out), .out(multiplexer_1_out), .sel(and_1_out));
  and and_1 (and_1_out, BR, Equals);
  Register #(.width(32)) register_1 (.D(adder_2_out), .Q(Addr), .clk(Clock), .clr(Reset));  // open: en
  Adder #(.width(32)) adder_2 (.a(multiplexer_1_out), .b(Addr), .out(adder_2_out));  // open: cin, cout

  // Notes on the sheet:
  //   Multiplica por 4
endmodule

module Computador (
  input  Reset,
  input  Clock
);

  wire [31:0] via_de_dados_1_addr, via_de_dados_1_instruction;

  Via_de_dados via_de_dados_1 (
    .Clock(Clock), .ADDR(via_de_dados_1_addr), .Instruction(via_de_dados_1_instruction));  // open: Reset, in_3
  MemRam memram_1 (.ADDR(via_de_dados_1_addr), .Instruction(via_de_dados_1_instruction));
endmodule
